// Logisim project SAP1.circ as structural Verilog: 14 circuits, main circuit main
module main (
);

  wire Clear_out, CLK, CLK_827b11c0, controller_1_ce_bfb99b38, controller_1_clr, controller_1_clr_9585ef7a,
       controller_1_cp, controller_1_ea, controller_1_ei_cec0510b, controller_1_ep, controller_1_eu,
       controller_1_la_10733fec, controller_1_lb_f268f6f6, controller_1_li_f87bbe4b,
       controller_1_lm_9a7bc5f2, controller_1_lo_4f046b9b, controller_1_su, dipswitch_1_sw1, Prog_Run_sw1,
       Step_out;
  wire [3:0] Instr;
  wire [6:0] outputregister_1_dsp1, outputregister_1_dsp2, outputregister_1_dsp3;
  wire [7:0] accumulator_1_wa, bregister_1_wb, programcounter_1_pc;

  Button Clear (.out(Clear_out));
  Button Step (.out(Step_out));
  // Probe on Instr
  DipSwitch #(.number(2)) dipswitch_1 (.sw1(dipswitch_1_sw1));  // open: sw2
  Controller controller_1 (
    .S5(Clear_out), .S6(Step_out), .S7(dipswitch_1_sw1), .IR(Instr), .CLR(controller_1_clr),
    .CLR_9585ef7a(controller_1_clr_9585ef7a), .CLK(CLK), .CLK_827b11c0(CLK_827b11c0), .Cp(controller_1_cp),
    .Ep(controller_1_ep), .Lm_9a7bc5f2(controller_1_lm_9a7bc5f2), .CE_bfb99b38(controller_1_ce_bfb99b38),
    .Li_f87bbe4b(controller_1_li_f87bbe4b), .Ei_cec0510b(controller_1_ei_cec0510b),
    .La_10733fec(controller_1_la_10733fec), .Ea(controller_1_ea), .Su(controller_1_su), .Eu(controller_1_eu),
    .Lb_f268f6f6(controller_1_lb_f268f6f6), .Lo_4f046b9b(controller_1_lo_4f046b9b));
  _7_Segment_Display u_7_segment_display_1 (
    .g(outputregister_1_dsp3[6]), .f(outputregister_1_dsp3[5]), .a(outputregister_1_dsp3[0]),
    .b(outputregister_1_dsp3[1]), .e(outputregister_1_dsp3[4]), .d(outputregister_1_dsp3[3]),
    .c(outputregister_1_dsp3[2]));  // open: dp
  DipSwitch #(.number(2)) Prog_Run (.sw1(Prog_Run_sw1));  // open: sw2
  _7_Segment_Display u_7_segment_display_2 (
    .g(outputregister_1_dsp2[6]), .f(outputregister_1_dsp2[5]), .a(outputregister_1_dsp2[0]),
    .b(outputregister_1_dsp2[1]), .e(outputregister_1_dsp2[4]), .d(outputregister_1_dsp2[3]),
    .c(outputregister_1_dsp2[2]));  // open: dp
  _7_Segment_Display u_7_segment_display_3 (
    .g(outputregister_1_dsp1[6]), .f(outputregister_1_dsp1[5]), .a(outputregister_1_dsp1[0]),
    .b(outputregister_1_dsp1[1]), .e(outputregister_1_dsp1[4]), .d(outputregister_1_dsp1[3]),
    .c(outputregister_1_dsp1[2]));  // open: dp
  ProgramCounter programcounter_1 (
    .Ep(controller_1_ep), .Cp(controller_1_cp), .CLK_caa0be3c(CLK_827b11c0),
    .CLR_d8c7be46(controller_1_clr_9585ef7a), .PC(programcounter_1_pc));
  MAR mar_1 (
    .WBus_in(programcounter_1_pc), .Lm_9136fd02(controller_1_lm_9a7bc5f2), .CLK(CLK),
    .CE_7076b96a(controller_1_ce_bfb99b38), .prog_run(Prog_Run_sw1), .WBus_out(programcounter_1_pc));
  InstructionRegister instructionregister_1 (
    .WBus_in(programcounter_1_pc), .Li_918300b3(controller_1_li_f87bbe4b), .CLK(CLK),
    .Ei_8cfcdd73(controller_1_ei_cec0510b), .CLR(controller_1_clr), .WBus_out(programcounter_1_pc),
    .IBus(Instr));
  // Probe on programcounter_1_pc
  Accumulator accumulator_1 (
    .WBus_in(programcounter_1_pc), .La_025e4b1e(controller_1_la_10733fec), .CLK(CLK), .Ea(controller_1_ea),
    .WBus_out(programcounter_1_pc), .WA(accumulator_1_wa));
  AdderSustractor addersustractor_1 (
    .WA(accumulator_1_wa), .WB(bregister_1_wb), .Su(controller_1_su), .Eu(controller_1_eu),
    .WBus_out(programcounter_1_pc));
  BRegister bregister_1 (
    .WBus_in(programcounter_1_pc), .CLK(CLK), .Lb_1955224c(controller_1_lb_f268f6f6), .WB(bregister_1_wb));
  OutputRegister outputregister_1 (
    .WBus_in(programcounter_1_pc), .CLK(CLK), .Lo_1b4e0d02(controller_1_lo_4f046b9b),
    .DSP3(outputregister_1_dsp3), .DSP2(outputregister_1_dsp2), .DSP1(outputregister_1_dsp1));

  // Notes on the sheet:
  //   Manual/Auto
endmodule

module Controller (
  input  S5,
  input  S6,
  input  S7,
  input  [3:0] IR,
  output CLR,
  output CLR_9585ef7a,
  output CLK,
  output CLK_827b11c0,
  output Cp,
  output Ep,
  output Lm_9a7bc5f2,
  output CE_bfb99b38,
  output Li_f87bbe4b,
  output Ei_cec0510b,
  output La_10733fec,
  output Ea,
  output Su,
  output Eu,
  output Lb_f268f6f6,
  output Lo_4f046b9b
);

  wire clock_1_out, debouncer_1_q, debouncer_2_q, debouncer_2_q_004d3fca, HLT_76c29af8,
       instrucciondecoder_1_add, instrucciondecoder_1_lda, instrucciondecoder_1_outt,
       instrucciondecoder_1_sub, j_k_ff_1_q, nand_1_out, nand_2_out, nand_3_out, not_1_out, not_2_out,
       not_3_out, not_4_out;
  wire [5:0] State;

  // Probe on State
  RingCounter ringcounter_1 (.CLK(CLK), .CLR(CLR_9585ef7a), .out_3(State));
  not not_1 (not_1_out, S6);
  not not_2 (not_2_out, S7);
  Clock clock_1 (.out(clock_1_out));
  J_K_Flip_Flop j_k_ff_1 (
    .J(HLT_76c29af8), .K(HLT_76c29af8), .clk(clock_1_out), .Q(j_k_ff_1_q), .reset(CLR));  // open: Qn, preset
  InstruccionDecoder instrucciondecoder_1 (
    .Instruction(IR), .LDA(instrucciondecoder_1_lda), .ADD(instrucciondecoder_1_add),
    .SUB(instrucciondecoder_1_sub), .OUTT(instrucciondecoder_1_outt), .HTL_86a13652(HLT_76c29af8));
  Debouncer debouncer_1 (.S(not_1_out), .R(S6), .Q(debouncer_1_q));  // open: Q_004d3fca
  Debouncer debouncer_2 (.S(not_2_out), .R(S7), .Q_004d3fca(debouncer_2_q_004d3fca), .Q(debouncer_2_q));
  // Probe on State
  not not_3 (not_3_out, S5);
  nand nand_1 (nand_1_out, HLT_76c29af8, debouncer_1_q, debouncer_2_q_004d3fca);
  nand nand_2 (nand_2_out, debouncer_2_q, j_k_ff_1_q);
  nand nand_3 (nand_3_out, nand_1_out, nand_2_out);
  ControlMatrix controlmatrix_1 (
    .T1(State[0]), .T2(State[1]), .T3(State[2]), .T4(State[3]), .LDA(instrucciondecoder_1_lda),
    .T5(State[4]), .ADD(instrucciondecoder_1_add), .T6(State[5]), .SUB(instrucciondecoder_1_sub),
    .iOUT(instrucciondecoder_1_outt), .Cp(Cp), .Ep(Ep), .Lm_9a7bc5f2(Lm_9a7bc5f2), .CE_bfb99b38(CE_bfb99b38),
    .Li_f87bbe4b(Li_f87bbe4b), .Ei_cec0510b(Ei_cec0510b), .La_10733fec(La_10733fec), .Ea(Ea), .Su(Su),
    .Eu(Eu), .Lb_f268f6f6(Lb_f268f6f6), .Lo_4f046b9b(Lo_4f046b9b));
  Debouncer debouncer_3 (.S(not_3_out), .R(S5), .Q_004d3fca(CLR), .Q(CLR_9585ef7a));
  not not_4 (not_4_out, nand_3_out);
  not not_5 (CLK, not_4_out);
  not not_6 (CLK_827b11c0, nand_3_out);
  // Probe on {Cp, Ep, Lm_9a7bc5f2, CE_bfb99b38, Li_f87bbe4b, Ei_cec0510b, La_10733fec, Ea, Su, Eu, Lb_f268f6f6, Lo_4f046b9b}

  // Other names for the same wires on the sheet: CLR_d8c7be46 = CLR_9585ef7a

  // Notes on the sheet:
  //   Single Step
  //   Manual/Auto
  //   Clock Circuit
  //   Ring Counter
  //   Clear/Start
  //   Control Word
endmodule

module RingCounter (
  input  CLK,
  input  CLR,
  output [5:0] out_3
);

  wire j_k_ff_1_q, j_k_ff_2_qn, j_k_ff_3_qn, j_k_ff_4_qn, j_k_ff_5_qn, j_k_ff_6_qn, not_1_out, not_2_out;

  not not_1 (not_1_out, CLK);
  not not_2 (not_2_out, CLR);
  J_K_Flip_Flop j_k_ff_1 (
    .J(j_k_ff_6_qn), .K(out_3[5]), .clk(not_1_out), .Q(j_k_ff_1_q), .Qn(out_3[0]), .reset(not_2_out));  // open: preset
  J_K_Flip_Flop j_k_ff_2 (
    .J(out_3[0]), .K(j_k_ff_1_q), .clk(not_1_out), .Q(out_3[1]), .Qn(j_k_ff_2_qn), .reset(not_2_out));  // open: preset
  J_K_Flip_Flop j_k_ff_3 (
    .J(out_3[1]), .K(j_k_ff_2_qn), .clk(not_1_out), .Q(out_3[2]), .Qn(j_k_ff_3_qn), .reset(not_2_out));  // open: preset
  J_K_Flip_Flop j_k_ff_4 (
    .J(out_3[2]), .K(j_k_ff_3_qn), .clk(not_1_out), .Q(out_3[3]), .Qn(j_k_ff_4_qn), .reset(not_2_out));  // open: preset
  J_K_Flip_Flop j_k_ff_5 (
    .J(out_3[3]), .K(j_k_ff_4_qn), .clk(not_1_out), .Q(out_3[4]), .Qn(j_k_ff_5_qn), .reset(not_2_out));  // open: preset
  J_K_Flip_Flop j_k_ff_6 (
    .J(out_3[4]), .K(j_k_ff_5_qn), .clk(not_1_out), .Q(out_3[5]), .Qn(j_k_ff_6_qn), .reset(not_2_out));  // open: preset
endmodule

module InstruccionDecoder (
  input  [3:0] Instruction,
  output LDA,
  output ADD,
  output SUB,
  output OUTT,
  output HTL_86a13652
);

  wire [3:0] not_1_out;

  assign not_1_out = ~Instruction;  // NOT_Gate not_1, 4 bits wide
  and and_1 (LDA, not_1_out[0], not_1_out[1], not_1_out[2], not_1_out[3]);
  and and_2 (ADD, Instruction[0], not_1_out[1], not_1_out[2], not_1_out[3]);
  and and_3 (SUB, not_1_out[0], Instruction[1], not_1_out[2], not_1_out[3]);
  and and_4 (OUTT, not_1_out[0], Instruction[1], Instruction[2], Instruction[3]);
  nand nand_1 (HTL_86a13652, Instruction[0], Instruction[3]);
endmodule

module ControlMatrix (
  input  T1,
  input  T2,
  input  T3,
  input  T4,
  input  LDA,
  input  T5,
  input  ADD,
  input  T6,
  input  SUB,
  input  iOUT,
  output Cp,
  output Ep,
  output Lm_9a7bc5f2,
  output CE_bfb99b38,
  output Li_f87bbe4b,
  output Ei_cec0510b,
  output La_10733fec,
  output Ea,
  output Su,
  output Eu,
  output Lb_f268f6f6,
  output Lo_4f046b9b
);

  wire and_1_out, and_2_out, and_3_out, and_4_out, and_5_out, and_6_out, and_7_out;

  and and_1 (and_1_out, T4, LDA);
  and and_2 (and_2_out, LDA, T5);
  and and_3 (and_3_out, T4, ADD);
  and and_4 (and_4_out, ADD, T5);
  and and_5 (and_5_out, ADD, T6);
  and and_6 (and_6_out, SUB, T4);
  and and_7 (and_7_out, T5, SUB);
  and and_8 (Su, T6, SUB);
  and and_9 (Ea, iOUT, T4);
  nor nor_1 (Lm_9a7bc5f2, T1, and_6_out, and_3_out, and_1_out);
  nor nor_2 (CE_bfb99b38, T3, and_7_out, and_4_out, and_2_out);
  not not_1 (Li_f87bbe4b, T3);
  nor nor_3 (Ei_cec0510b, and_1_out, and_3_out, and_6_out);
  nor nor_4 (La_10733fec, and_2_out, Su, and_5_out);
  or or_1 (Eu, and_5_out, Su);
  nor nor_5 (Lb_f268f6f6, and_4_out, and_7_out);
  not not_2 (Lo_4f046b9b, Ea);

  assign Cp = T2;
  assign Ep = T1;
endmodule

module Debouncer (
  input  S,
  input  R,
  output Q_004d3fca,
  output Q
);

  nand nand_1 (Q_004d3fca, S, Q);
  nand nand_2 (Q, Q_004d3fca, R);
endmodule

module InstructionRegister (
  input  [7:0] WBus_in,
  input  Li_918300b3,
  input  CLK,
  input  Ei_8cfcdd73,
  input  CLR,
  output [7:0] WBus_out,
  output [3:0] IBus
);

  wire [3:0] c74ls173_1_p, c74ls173_2_p;

  // Probe on WBus_in[7:4]
  // Probe on WBus_in[3:0]
  c74LS173 c74ls173_1 (
    .D(WBus_in[3:0]), .CLK_7(CLK), .G1_9_198a68ec(Li_918300b3), .G2_10_44a33287(Li_918300b3), .CLR_15(1'b0),
    .M_1(Ei_8cfcdd73), .N_2(Ei_8cfcdd73), .Q(WBus_out[3:0]), .P(c74ls173_1_p));
  // Probe on c74ls173_1_p
  c74LS173 c74ls173_2 (
    .D(WBus_in[7:4]), .CLK_7(CLK), .G1_9_198a68ec(Li_918300b3), .G2_10_44a33287(Li_918300b3), .CLR_15(CLR),
    .M_1(1'b0), .N_2(1'b0), .Q(IBus), .P(c74ls173_2_p));
  // Probe on c74ls173_2_p
endmodule

module ProgramCounter (
  input  Ep,
  input  Cp,
  input  CLK_caa0be3c,
  input  CLR_d8c7be46,
  output [7:0] PC
);

  wire not_1_out, not_2_out, not_3_out, not_4_out, not_5_out;
  wire [7:0] c74LS126_q;

  not not_1 (not_1_out, CLK_caa0be3c);
  not not_2 (not_2_out, CLR_d8c7be46);
  J_K_Flip_Flop c74LS126 (.J(Cp), .K(Cp), .clk(not_1_out), .Q(c74LS126_q[0]), .reset(not_2_out));  // open: Qn, preset
  not not_3 (not_3_out, c74LS126_q[0]);
  J_K_Flip_Flop j_k_ff_1 (.J(Cp), .K(Cp), .clk(not_3_out), .Q(c74LS126_q[1]), .reset(not_2_out));  // open: Qn, preset
  not not_4 (not_4_out, c74LS126_q[1]);
  J_K_Flip_Flop j_k_ff_2 (.J(Cp), .K(Cp), .clk(not_4_out), .Q(c74LS126_q[2]), .reset(not_2_out));  // open: Qn, preset
  not not_5 (not_5_out, c74LS126_q[2]);
  J_K_Flip_Flop j_k_ff_3 (.J(Cp), .K(Cp), .clk(not_5_out), .Q(c74LS126_q[3]), .reset(not_2_out));  // open: Qn, preset
  // Probe on c74LS126_q
  assign PC = Ep ? c74LS126_q : 8'bz;  // Controlled_Buffer controlled_buffer_1
endmodule

module MAR (
  input  [7:0] WBus_in,
  input  Lm_9136fd02,
  input  CLK,
  input  CE_7076b96a,
  input  prog_run,
  output [7:0] WBus_out
);

  wire multiplexer_2_out, not_1_out, not_2_out, not_3_out, not_4_out, WRITE_sw1;
  wire [3:0] ADDRESS_sw4, c74LS173_q, controlled_buffer_1_out, multiplexer_1_out;
  wire [7:0] c74189_dout, DATA_sw8;

  not not_1 (not_1_out, Lm_9136fd02);
  not not_2 (not_2_out, CLK);
  // Probe on controlled_buffer_1_out
  assign controlled_buffer_1_out = not_1_out ? WBus_in[3:0] : 4'bz;  // Controlled_Buffer controlled_buffer_1
  DipSwitch #(.number(4)) ADDRESS (
    .sw1(ADDRESS_sw4[3]), .sw2(ADDRESS_sw4[2]), .sw3(ADDRESS_sw4[1]), .sw4(ADDRESS_sw4[0]));
  // Probe on c74LS173_q
  Register #(.width(4)) c74LS173 (.D(controlled_buffer_1_out), .en(not_1_out), .clk(CLK), .Q(c74LS173_q), .clr(1'b0));
  // Probe on multiplexer_1_out
  not not_3 (not_3_out, prog_run);
  DipSwitch #(.number(2)) WRITE (.sw1(WRITE_sw1));  // open: sw2
  Multiplexer #(.width(4), .enable("false")) multiplexer_1 (
    .in0(ADDRESS_sw4), .in1(c74LS173_q), .out(multiplexer_1_out), .sel(not_3_out));
  not not_4 (not_4_out, multiplexer_2_out);
  Multiplexer #(.enable("false")) multiplexer_2 (
    .in0(1'b0), .in1(CE_7076b96a), .out(multiplexer_2_out), .sel(not_3_out));
  DipSwitch DATA (
    .sw1(DATA_sw8[7]), .sw2(DATA_sw8[6]), .sw3(DATA_sw8[5]), .sw4(DATA_sw8[4]), .sw5(DATA_sw8[3]),
    .sw6(DATA_sw8[2]), .sw7(DATA_sw8[1]), .sw8(DATA_sw8[0]));
  RAM #(.addrWidth(4), .databus("bibus")) c74189 (
    .addr(multiplexer_1_out), .we(WRITE_sw1), .oe(not_4_out), .clk(not_2_out), .din(DATA_sw8),
    .dout(c74189_dout));
  assign WBus_out = not_4_out ? c74189_dout : 8'bz;  // Controlled_Buffer controlled_buffer_2
  // Probe on c74189_dout

  // Notes on the sheet:
  //   c74LS157
endmodule

module Accumulator (
  input  [7:0] WBus_in,
  input  La_025e4b1e,
  input  CLK,
  input  Ea,
  output [7:0] WBus_out,
  output [7:0] WA
);

  wire not_1_out;

  // Probe on WBus_in[7:4]
  // Probe on WBus_in[3:0]
  not not_1 (not_1_out, Ea);
  c74LS173 c74ls173_1 (
    .D(WBus_in[3:0]), .CLK_7(CLK), .G1_9_198a68ec(La_025e4b1e), .G2_10_44a33287(La_025e4b1e), .CLR_15(1'b0),
    .M_1(not_1_out), .N_2(not_1_out), .Q(WBus_out[3:0]), .P(WA[3:0]));
  c74LS173 c74ls173_2 (
    .D(WBus_in[7:4]), .CLK_7(CLK), .G1_9_198a68ec(La_025e4b1e), .G2_10_44a33287(La_025e4b1e), .CLR_15(1'b0),
    .M_1(not_1_out), .N_2(not_1_out), .Q(WBus_out[7:4]), .P(WA[7:4]));
endmodule

module AdderSustractor (
  input  [7:0] WA,
  input  [7:0] WB,
  input  Su,
  input  Eu,
  output [7:0] WBus_out
);

  wire [7:0] adder_1_out, bit_extender_1_out, xor_1_out;

  assign bit_extender_1_out = {{7{Su}}, Su};  // Bit_Extender bit_extender_1
  assign xor_1_out = WB ^ bit_extender_1_out;  // XOR_Gate xor_1, 8 bits wide
  // Probe on bit_extender_1_out
  // Probe on adder_1_out
  Adder adder_1 (.a(WA), .b(xor_1_out), .out(adder_1_out), .cin(Su));  // open: cout
  assign WBus_out = Eu ? adder_1_out : 8'bz;  // Controlled_Buffer controlled_buffer_1
endmodule

module BRegister (
  input  [7:0] WBus_in,
  input  CLK,
  input  Lb_1955224c,
  output [7:0] WB
);

  c74LS173 c74ls173_1 (
    .D(WBus_in[3:0]), .CLK_7(CLK), .G1_9_198a68ec(Lb_1955224c), .G2_10_44a33287(Lb_1955224c), .CLR_15(1'b0),
    .M_1(1'b0), .N_2(1'b0), .Q(WB[3:0]));  // open: P
  c74LS173 c74ls173_2 (
    .D(WBus_in[7:4]), .CLK_7(CLK), .G1_9_198a68ec(Lb_1955224c), .G2_10_44a33287(Lb_1955224c), .CLR_15(1'b0),
    .M_1(1'b0), .N_2(1'b0), .Q(WB[7:4]));  // open: P
endmodule

module OutputRegister (
  input  [7:0] WBus_in,
  input  CLK,
  input  Lo_1b4e0d02,
  output [6:0] DSP3,
  output [6:0] DSP2,
  output [6:0] DSP1
);

  wire bcd_to_7_segment_decoder_1_p5, binairy_to_bcd_converter_1_p3, binairy_to_bcd_converter_1_p4;
  wire [3:0] c74ls173_1_q, c74ls173_2_q;

  c74LS173 c74ls173_1 (
    .D(WBus_in[3:0]), .CLK_7(CLK), .G1_9_198a68ec(Lo_1b4e0d02), .G2_10_44a33287(Lo_1b4e0d02), .CLR_15(1'b0),
    .M_1(1'b0), .N_2(1'b0), .Q(c74ls173_1_q));  // open: P
  c74LS173 c74ls173_2 (
    .D(WBus_in[7:4]), .CLK_7(CLK), .G1_9_198a68ec(Lo_1b4e0d02), .G2_10_44a33287(Lo_1b4e0d02), .CLR_15(1'b0),
    .M_1(1'b0), .N_2(1'b0), .Q(c74ls173_2_q));  // open: P
  // BCD_to_7_Segment_decoder bcd_to_7_segment_decoder_1: pin names not known; wires that end beside it: DSP3[6], DSP3[4], DSP3[5], DSP3[3], bcd_to_7_segment_decoder_1_p5, DSP3[0], DSP3[2], DSP3[1]
  // Binairy_to_BCD_converter #(.binvalue(8)) binairy_to_bcd_converter_1: pin names not known; wires that end beside it: {c74ls173_2_q, c74ls173_1_q}, bcd_to_7_segment_decoder_1_p5, binairy_to_bcd_converter_1_p3, binairy_to_bcd_converter_1_p4
  // BCD_to_7_Segment_decoder bcd_to_7_segment_decoder_2: pin names not known; wires that end beside it: DSP2[6], DSP2[4], DSP2[5], DSP2[3], binairy_to_bcd_converter_1_p3, DSP2[0], DSP2[2], DSP2[1]
  // BCD_to_7_Segment_decoder bcd_to_7_segment_decoder_3: pin names not known; wires that end beside it: DSP1[6], DSP1[4], DSP1[5], DSP1[3], binairy_to_bcd_converter_1_p4, DSP1[0], DSP1[2], DSP1[1]
endmodule

module c74LS173 (
  input  [3:0] D,
  input  CLK_7,
  input  G1_9_198a68ec,
  input  G2_10_44a33287,
  input  CLR_15,
  input  M_1,
  input  N_2,
  output [3:0] Q,
  output [3:0] P
);

  wire nor_1_out, nor_2_out;
  wire [3:0] controlled_buffer_1_out;

  // Probe on controlled_buffer_1_out
  assign controlled_buffer_1_out = nor_1_out ? D : 4'bz;  // Controlled_Buffer controlled_buffer_1
  nor nor_1 (nor_1_out, G1_9_198a68ec, G2_10_44a33287);
  Register #(.width(4)) register_1 (.D(controlled_buffer_1_out), .en(nor_1_out), .clk(CLK_7), .Q(P), .clr(CLR_15));
  // Probe on P
  nor nor_2 (nor_2_out, M_1, N_2);
  assign Q = nor_2_out ? P : 4'bz;  // Controlled_Buffer controlled_buffer_2
endmodule
