// Logisim project SAP1.circ as structural Verilog: 11 circuits, main circuit main
module main (
  output [7:0] out_1
);

  wire Clear_out, CLK, CLK_827b11c0, controller_1_ce_bfb99b38, controller_1_clr, controller_1_clr_9585ef7a,
       controller_1_cp, controller_1_ei_cec0510b, controller_1_ep, controller_1_li_f87bbe4b,
       controller_1_lm_9a7bc5f2, dipswitch_1_sw1, Prog_Run_sw1, Step_out;
  wire [3:0] instructionregister_1_ibus;

  DipSwitch #(.number(2)) dipswitch_1 (.sw1(dipswitch_1_sw1));  // open: sw2
  Button Clear (.out(Clear_out));
  Button Step (.out(Step_out));
  Controller controller_1 (
    .S5(Clear_out), .S6(Step_out), .S7(dipswitch_1_sw1), .IR(instructionregister_1_ibus),
    .CLR(controller_1_clr), .CLR_9585ef7a(controller_1_clr_9585ef7a), .CLK(CLK), .CLK_827b11c0(CLK_827b11c0),
    .Cp(controller_1_cp), .Ep(controller_1_ep), .Lm_9a7bc5f2(controller_1_lm_9a7bc5f2),
    .CE_bfb99b38(controller_1_ce_bfb99b38), .Li_f87bbe4b(controller_1_li_f87bbe4b),
    .Ei_cec0510b(controller_1_ei_cec0510b));  // open: La_10733fec, Ea, Su, Eu, Lb_f268f6f6, Lo_4f046b9b
  DipSwitch #(.number(2)) Prog_Run (.sw1(Prog_Run_sw1));  // open: sw2
  // Probe on out_1
  ProgramCounter programcounter_1 (
    .Ep(controller_1_ep), .Cp(controller_1_cp), .CLK_caa0be3c(CLK_827b11c0),
    .CLR_d8c7be46(controller_1_clr_9585ef7a), .PC(out_1));
  // Probe on instructionregister_1_ibus
  MAR mar_1 (
    .WBus_in(out_1), .Lm_9136fd02(controller_1_lm_9a7bc5f2), .CLK(CLK),
    .CE_7076b96a(controller_1_ce_bfb99b38), .prog_run(Prog_Run_sw1), .WBus_out(out_1));
  InstructionRegister instructionregister_1 (
    .WBus_in(out_1), .Li_918300b3(controller_1_li_f87bbe4b), .CLK(CLK),
    .Ei_8cfcdd73(controller_1_ei_cec0510b), .CLR(controller_1_clr), .WBus_out(out_1),
    .IBus(instructionregister_1_ibus));

  // Notes on the sheet:
  //   Manual/Auto
endmodule

module Controller (
  input  S5,
  input  S6,
  input  S7,
  input  [3:0] IR,
  output CLR,
  output CLR_9585ef7a,
  output CLK,
  output CLK_827b11c0,
  output Cp,
  output Ep,
  output Lm_9a7bc5f2,
  output CE_bfb99b38,
  output Li_f87bbe4b,
  output Ei_cec0510b,
  output La_10733fec,
  output Ea,
  output Su,
  output Eu,
  output Lb_f268f6f6,
  output Lo_4f046b9b
);

  wire clock_1_out, debouncer_1_q, debouncer_2_q, debouncer_2_q_004d3fca, HLT_76c29af8,
       instrucciondecoder_1_add, instrucciondecoder_1_lda, instrucciondecoder_1_outt,
       instrucciondecoder_1_sub, j_k_ff_1_q, nand_1_out, nand_2_out, nand_3_out, not_1_out, not_2_out,
       not_3_out, not_4_out;
  wire [5:0] State;

  // Probe on State
  RingCounter ringcounter_1 (.CLK(CLK), .CLR(CLR_9585ef7a), .out_3(State));
  not not_1 (not_1_out, S6);
  not not_2 (not_2_out, S7);
  Clock clock_1 (.out(clock_1_out));
  J_K_Flip_Flop j_k_ff_1 (
    .J(HLT_76c29af8), .K(HLT_76c29af8), .clk(clock_1_out), .Q(j_k_ff_1_q), .reset(CLR));  // open: Qn, preset
  InstruccionDecoder instrucciondecoder_1 (
    .Instruction(IR), .LDA(instrucciondecoder_1_lda), .ADD(instrucciondecoder_1_add),
    .SUB(instrucciondecoder_1_sub), .OUTT(instrucciondecoder_1_outt), .HTL_86a13652(HLT_76c29af8));
  Debouncer debouncer_1 (.S(not_1_out), .R(S6), .Q(debouncer_1_q));  // open: Q_004d3fca
  Debouncer debouncer_2 (.S(not_2_out), .R(S7), .Q_004d3fca(debouncer_2_q_004d3fca), .Q(debouncer_2_q));
  // Probe on State
  not not_3 (not_3_out, S5);
  nand nand_1 (nand_1_out, HLT_76c29af8, debouncer_1_q, debouncer_2_q_004d3fca);
  nand nand_2 (nand_2_out, debouncer_2_q, j_k_ff_1_q);
  nand nand_3 (nand_3_out, nand_1_out, nand_2_out);
  ControlMatrix controlmatrix_1 (
    .T1(State[0]), .T2(State[1]), .T3(State[2]), .T4(State[3]), .LDA(instrucciondecoder_1_lda),
    .T5(State[4]), .ADD(instrucciondecoder_1_add), .T6(State[5]), .SUB(instrucciondecoder_1_sub),
    .iOUT(instrucciondecoder_1_outt), .Cp(Cp), .Ep(Ep), .Lm_9a7bc5f2(Lm_9a7bc5f2), .CE_bfb99b38(CE_bfb99b38),
    .Li_f87bbe4b(Li_f87bbe4b), .Ei_cec0510b(Ei_cec0510b), .La_10733fec(La_10733fec), .Ea(Ea), .Su(Su),
    .Eu(Eu), .Lb_f268f6f6(Lb_f268f6f6), .Lo_4f046b9b(Lo_4f046b9b));
  Debouncer debouncer_3 (.S(not_3_out), .R(S5), .Q_004d3fca(CLR), .Q(CLR_9585ef7a));
  not not_4 (not_4_out, nand_3_out);
  not not_5 (CLK, not_4_out);
  not not_6 (CLK_827b11c0, nand_3_out);
  // Probe on {Cp, Ep, Lm_9a7bc5f2, CE_bfb99b38, Li_f87bbe4b, Ei_cec0510b, La_10733fec, Ea, Su, Eu, Lb_f268f6f6, Lo_4f046b9b}

  // Other names for the same wires on the sheet: CLR_d8c7be46 = CLR_9585ef7a

  // Notes on the sheet:
  //   Single Step
  //   Manual/Auto
  //   Clock Circuit
  //   Ring Counter
  //   Clear/Start
  //   Control Word
endmodule

module RingCounter (
  input  CLK,
  input  CLR,
  output [5:0] out_3
);

  wire j_k_ff_1_q, j_k_ff_2_qn, j_k_ff_3_qn, j_k_ff_4_qn, j_k_ff_5_qn, j_k_ff_6_qn, not_1_out, not_2_out;

  not not_1 (not_1_out, CLK);
  not not_2 (not_2_out, CLR);
  J_K_Flip_Flop j_k_ff_1 (
    .J(j_k_ff_6_qn), .K(out_3[5]), .clk(not_1_out), .Q(j_k_ff_1_q), .Qn(out_3[0]), .reset(not_2_out));  // open: preset
  J_K_Flip_Flop j_k_ff_2 (
    .J(out_3[0]), .K(j_k_ff_1_q), .clk(not_1_out), .Q(out_3[1]), .Qn(j_k_ff_2_qn), .reset(not_2_out));  // open: preset
  J_K_Flip_Flop j_k_ff_3 (
    .J(out_3[1]), .K(j_k_ff_2_qn), .clk(not_1_out), .Q(out_3[2]), .Qn(j_k_ff_3_qn), .reset(not_2_out));  // open: preset
  J_K_Flip_Flop j_k_ff_4 (
    .J(out_3[2]), .K(j_k_ff_3_qn), .clk(not_1_out), .Q(out_3[3]), .Qn(j_k_ff_4_qn), .reset(not_2_out));  // open: preset
  J_K_Flip_Flop j_k_ff_5 (
    .J(out_3[3]), .K(j_k_ff_4_qn), .clk(not_1_out), .Q(out_3[4]), .Qn(j_k_ff_5_qn), .reset(not_2_out));  // open: preset
  J_K_Flip_Flop j_k_ff_6 (
    .J(out_3[4]), .K(j_k_ff_5_qn), .clk(not_1_out), .Q(out_3[5]), .Qn(j_k_ff_6_qn), .reset(not_2_out));  // open: preset
endmodule

module InstructionRegister (
  input  [7:0] WBus_in,
  input  Li_918300b3,
  input  CLK,
  input  Ei_8cfcdd73,
  input  CLR,
  output [7:0] WBus_out,
  output [3:0] IBus
);

  // Probe on WBus_in[7:4]
  // Probe on WBus_in[3:0]
  c74LS173 c74ls173_1 (
    .D(WBus_in[3:0]), .CLK_7(CLK), .G1_9_198a68ec(Li_918300b3), .G2_10_44a33287(Li_918300b3), .CLR_15(1'b0),
    .M_1(Ei_8cfcdd73), .N_2(Ei_8cfcdd73), .Q(WBus_out[3:0]));
  c74LS173 c74ls173_2 (
    .D(WBus_in[7:4]), .CLK_7(CLK), .G1_9_198a68ec(Li_918300b3), .G2_10_44a33287(Li_918300b3), .CLR_15(CLR),
    .M_1(1'b0), .N_2(1'b0), .Q(IBus));
endmodule

module ProgramCounter (
  input  Ep,
  input  Cp,
  input  CLK_caa0be3c,
  input  CLR_d8c7be46,
  output [7:0] PC
);

  wire not_1_out, not_2_out, not_3_out, not_4_out, not_5_out;
  wire [7:0] c74LS126_q;

  not not_1 (not_1_out, CLK_caa0be3c);
  not not_2 (not_2_out, CLR_d8c7be46);
  J_K_Flip_Flop c74LS126 (.J(Cp), .K(Cp), .clk(not_1_out), .Q(c74LS126_q[0]), .reset(not_2_out));  // open: Qn, preset
  not not_3 (not_3_out, c74LS126_q[0]);
  J_K_Flip_Flop j_k_ff_1 (.J(Cp), .K(Cp), .clk(not_3_out), .Q(c74LS126_q[1]), .reset(not_2_out));  // open: Qn, preset
  not not_4 (not_4_out, c74LS126_q[1]);
  J_K_Flip_Flop j_k_ff_2 (.J(Cp), .K(Cp), .clk(not_4_out), .Q(c74LS126_q[2]), .reset(not_2_out));  // open: Qn, preset
  not not_5 (not_5_out, c74LS126_q[2]);
  J_K_Flip_Flop j_k_ff_3 (.J(Cp), .K(Cp), .clk(not_5_out), .Q(c74LS126_q[3]), .reset(not_2_out));  // open: Qn, preset
  // Probe on c74LS126_q
  assign PC = Ep ? c74LS126_q : 8'bz;  // Controlled_Buffer controlled_buffer_1
endmodule

module MAR (
  input  [7:0] WBus_in,
  input  Lm_9136fd02,
  input  CLK,
  input  CE_7076b96a,
  input  prog_run,
  output [7:0] WBus_out
);

  wire multiplexer_2_out, not_1_out, not_2_out, not_3_out, WRITE_sw1;
  wire [3:0] ADDRESS_sw4, c74LS173_q, controlled_buffer_1_out, multiplexer_1_out;
  wire [7:0] c74189_dout, DATA_sw8;

  not not_1 (not_1_out, Lm_9136fd02);
  // Probe on controlled_buffer_1_out
  assign controlled_buffer_1_out = not_1_out ? WBus_in[3:0] : 4'bz;  // Controlled_Buffer controlled_buffer_1
  DipSwitch #(.number(4)) ADDRESS (
    .sw1(ADDRESS_sw4[3]), .sw2(ADDRESS_sw4[2]), .sw3(ADDRESS_sw4[1]), .sw4(ADDRESS_sw4[0]));
  // Probe on c74LS173_q
  Register #(.width(4)) c74LS173 (.D(controlled_buffer_1_out), .en(not_1_out), .clk(CLK), .Q(c74LS173_q), .clr(1'b0));
  // Probe on multiplexer_1_out
  not not_2 (not_2_out, prog_run);
  DipSwitch #(.number(2)) WRITE (.sw1(WRITE_sw1));  // open: sw2
  Multiplexer #(.width(4), .enable("false")) multiplexer_1 (
    .in0(ADDRESS_sw4), .in1(c74LS173_q), .out(multiplexer_1_out), .sel(not_2_out));
  not not_3 (not_3_out, multiplexer_2_out);
  Multiplexer #(.enable("false")) multiplexer_2 (
    .in0(1'b0), .in1(CE_7076b96a), .out(multiplexer_2_out), .sel(not_2_out));
  DipSwitch DATA (
    .sw1(DATA_sw8[7]), .sw2(DATA_sw8[6]), .sw3(DATA_sw8[5]), .sw4(DATA_sw8[4]), .sw5(DATA_sw8[3]),
    .sw6(DATA_sw8[2]), .sw7(DATA_sw8[1]), .sw8(DATA_sw8[0]));
  RAM #(.addrWidth(4), .databus("bibus")) c74189 (
    .addr(multiplexer_1_out), .we(WRITE_sw1), .oe(not_3_out), .clk(CLK), .din(DATA_sw8), .dout(c74189_dout));
  assign WBus_out = not_3_out ? c74189_dout : 8'bz;  // Controlled_Buffer controlled_buffer_2
  // Probe on c74189_dout

  // Notes on the sheet:
  //   c74LS157
endmodule

module c74LS173 (
  input  [3:0] D,
  input  CLK_7,
  input  G1_9_198a68ec,
  input  G2_10_44a33287,
  input  CLR_15,
  input  M_1,
  input  N_2,
  output [3:0] Q
);

  wire nor_1_out, nor_2_out;
  wire [3:0] controlled_buffer_1_out, register_1_q;

  // Probe on controlled_buffer_1_out
  assign controlled_buffer_1_out = nor_1_out ? D : 4'bz;  // Controlled_Buffer controlled_buffer_1
  nor nor_1 (nor_1_out, G1_9_198a68ec, G2_10_44a33287);
  Register #(.width(4)) register_1 (
    .D(controlled_buffer_1_out), .en(nor_1_out), .clk(CLK_7), .Q(register_1_q), .clr(CLR_15));
  // Probe on register_1_q
  nor nor_2 (nor_2_out, M_1, N_2);
  assign Q = nor_2_out ? register_1_q : 4'bz;  // Controlled_Buffer controlled_buffer_2
endmodule

module Debouncer (
  input  S,
  input  R,
  output Q_004d3fca,
  output Q
);

  nand nand_1 (Q_004d3fca, S, Q);
  nand nand_2 (Q, Q_004d3fca, R);
endmodule

module InstruccionDecoder (
  input  [3:0] Instruction,
  output LDA,
  output ADD,
  output SUB,
  output OUTT,
  output HTL_86a13652
);

  wire [3:0] not_1_out;

  assign not_1_out = ~Instruction;  // NOT_Gate not_1, 4 bits wide
  and and_1 (LDA, not_1_out[0], not_1_out[1], not_1_out[2], not_1_out[3]);
  and and_2 (ADD, Instruction[0], not_1_out[1], not_1_out[2], not_1_out[3]);
  and and_3 (SUB, not_1_out[0], Instruction[1], not_1_out[2], not_1_out[3]);
  and and_4 (OUTT, not_1_out[0], Instruction[1], Instruction[2], Instruction[3]);
  nand nand_1 (HTL_86a13652, Instruction[0], Instruction[3]);
endmodule

module ControlMatrix (
  input  T1,
  input  T2,
  input  T3,
  input  T4,
  input  LDA,
  input  T5,
  input  ADD,
  input  T6,
  input  SUB,
  input  iOUT,
  output Cp,
  output Ep,
  output Lm_9a7bc5f2,
  output CE_bfb99b38,
  output Li_f87bbe4b,
  output Ei_cec0510b,
  output La_10733fec,
  output Ea,
  output Su,
  output Eu,
  output Lb_f268f6f6,
  output Lo_4f046b9b
);

  wire and_1_out, and_2_out, and_3_out, and_4_out, and_5_out, and_6_out, and_7_out;

  and and_1 (and_1_out, T4, LDA);
  and and_2 (and_2_out, LDA, T5);
  and and_3 (and_3_out, T4, ADD);
  and and_4 (and_4_out, ADD, T5);
  and and_5 (and_5_out, ADD, T6);
  and and_6 (and_6_out, SUB, T4);
  and and_7 (and_7_out, T5, SUB);
  and and_8 (Su, T6, SUB);
  and and_9 (Ea, iOUT, T4);
  nor nor_1 (Lm_9a7bc5f2, T1, and_6_out, and_3_out, and_1_out);
  nor nor_2 (CE_bfb99b38, T3, and_7_out, and_4_out, and_2_out);
  not not_1 (Li_f87bbe4b, T3);
  nor nor_3 (Ei_cec0510b, and_1_out, and_3_out, and_6_out);
  nor nor_4 (La_10733fec, and_2_out, Su, and_5_out);
  or or_1 (Eu, and_5_out, Su);
  nor nor_5 (Lb_f268f6f6, and_4_out, and_7_out);
  not not_2 (Lo_4f046b9b, Ea);

  assign Cp = T2;
  assign Ep = T1;
endmodule

module Accumulator (
  input  [7:0] in_1,
  input  La_,
  input  CLK,
  input  Ea,
  output [7:0] out_5
);

  // Probe on in_1[7:4]
  // Probe on in_1[3:0]
  c74LS173 c74ls173_1 (
    .D(in_1[3:0]), .CLK_7(CLK), .G1_9_198a68ec(La_), .G2_10_44a33287(La_), .CLR_15(1'b0), .M_1(Ea), .N_2(Ea),
    .Q(out_5[3:0]));
  c74LS173 c74ls173_2 (
    .D(in_1[7:4]), .CLK_7(CLK), .G1_9_198a68ec(La_), .G2_10_44a33287(La_), .CLR_15(1'b0), .M_1(Ea), .N_2(Ea),
    .Q(out_5[7:4]));
endmodule
